# Fritzing sketch Header Shield (saved by Fritzing 0.9.3b)
stripboards: 1

parts:
  JP3 = Header 8 [package=1x08_smd]
  JP4 = Header 10 [package=1x10-2mm-smd]
  JP5 = Header 6 [package=1x06_smd_straight_alt]
  JP6 = Header 8 [package=1x08_smd]
  JP7 = Header 2 [package=molex-1x2_lock]  # not connected
  JP8 = Header 2 [package=molex-1x2_lock]  # not connected
  JP9 = Header 2 [package=molex-1x2_lock]  # not connected
  JP10 = Header 2 [package=molex-1x2_lock]
  JP11 = Header 2 [package=molex-1x2_lock]  # not connected
  JP12 = Header 2 [package=molex-1x2_lock]
  JP13 = Header 2 [package=molex-1x2_lock]
  JP14 = Header 2 [package=molex-1x2_lock]
  JP15 = Header 2 [package=molex-1x2_lock]

nets:
  N1: JP3.1, JP3.2, JP3.3, JP3.4, JP3.5, JP3.6, JP3.7, JP3.8, JP4.1, JP4.2, JP4.3, JP4.4, JP4.5, JP4.6, JP4.7, JP4.8, JP4.9, JP4.10
  N2: JP5.1, JP5.2, JP5.3, JP5.4, JP5.5, JP5.6
  N3: JP6.1, JP6.2, JP6.3, JP6.4, JP6.5, JP6.6, JP6.7, JP6.8
  N4: JP10.1, JP12.2
  N5: JP10.2, JP12.1
  N6: JP13.1, JP13.2, JP14.1, JP14.2, JP15.2
