# Fritzing sketch Monster_In_A_Box (saved by Fritzing 0.9.3b)

parts:
  Part1 = Arduino Uno (Rev3) - ICSP
  S2 = Round Pushbutton
  PIR1 = PIR sensor
  U1 = 4-Channel 5v Relay Shield [package=relay-4ch5v10a]
  M1 = DC Motor
  LED2 = LED - 5mm [color="Red (633nm)" package="5 mm [THT]"]
  S3 = Round Pushbutton
  LED3 = LED - 5mm [color="Red (633nm)" package="5 mm [THT]"]
  LED4 = LED - 5mm [color="Red (633nm)" package="5 mm [THT]"]
  LED5 = LED - 5mm [color="Red (633nm)" package="5 mm [THT]"]
  LED6 = LED - 5mm [color="Red (633nm)" package="5 mm [THT]"]  # not connected
  LED7 = LED - 5mm [color="Red (633nm)" package="5 mm [THT]"]  # not connected

nets:
  N1: Part1.A0, PIR1.SIG
  N2: Part1.A1, LED5.anode
  N3: Part1.A2, LED4.anode
  N4: Part1.A3, LED3.anode
  N5: Part1.A4/SDA, S3.leg0
  N6: Part1.A5/SCL, S2.leg0
  N7: Part1.D8, U1.IN1
  N8: Part1.D6_PWM, U1.IN3
  N9: Part1.D7, U1.IN2
  3V3: Part1.3V3, PIR1.VDD
  5V: Part1.5V, U1.VCC
  GND: Part1.GND, PIR1.GND
  N10: U1.K1-On, M1.pin_2
  N11: U1.K2-Off, LED2.cathode

notes:
  String of Red
  LED Mini Lights
  Wiper
  Motor
  12 volts
  DC
  120 volts
  AC
  FOG MACHINE
  5 volts
  DC
  PIR Motion Sensor
  Pause
  (latching)
  Paused LED
  Debug
  (latching)
  NOTE:
  Wave Shield
  Not Shown
  Ready to Wake LED
  Motion Detected LED
  Wave Shield Uses Pins: 2, 3, 4, 5, 10, 11, 12 & 13

custom parts:
  4-Channel 5v Relay Shield: 4 Channel 5v Relay Shield w. 2x SPD-06VDC-SD-C
